// Logisim project Modulo codificador em Morse.circ as structural Verilog: 1 circuit, main circuit main
module main (
  input  in_1,
  input  in_2,
  input  in_3,
  input  in_4,
  output S1,
  output S2,
  output S3,
  output S4,
  output S5
);

  wire and_1_out, and_2_out, and_3_out, and_4_out, and_5_out, and_6_out, and_7_out, and_8_out, and_9_out,
       and_10_out, not_1_out, not_2_out, not_3_out, not_4_out;

  not not_1 (not_1_out, in_2);
  not not_2 (not_2_out, in_1);
  not not_3 (not_3_out, in_3);
  not not_4 (not_4_out, in_4);
  and and_1 (and_1_out, not_1_out, in_3);
  and and_2 (and_2_out, in_2, not_3_out);
  and and_3 (and_3_out, not_2_out, not_1_out, in_4);
  and and_4 (and_4_out, not_1_out, in_3);
  and and_5 (and_5_out, in_3, not_4_out);
  and and_6 (and_6_out, in_2, not_3_out);
  and and_7 (and_7_out, in_3, in_4);
  and and_8 (and_8_out, in_1, not_4_out);
  and and_9 (and_9_out, in_2, in_4);
  and and_10 (and_10_out, in_2, in_3);
  or or_1 (S1, and_1_out, and_2_out, and_3_out);
  or or_2 (S2, and_4_out, and_5_out, and_6_out);
  or or_3 (S3, in_2, and_7_out);
  or or_4 (S4, in_2, and_8_out);
  or or_5 (S5, in_1, and_9_out, and_10_out);

  // Notes on the sheet:
  //   A          B         C          D      
endmodule
